# Fritzing sketch 555_DESIGN (saved by Fritzing 0.9.3b)

parts:
  U1 = 555 Timer [package="DIP8 [THT]"]
  L1 = Inductor [package="0603 [SMD]"]
  R1 = Resistor [tolerance=±5% resistance=3.3k package=THT]
  C1 = Electrolytic Capacitor [capacitance=10µF package="100 mil [THT, electrolytic]"]
  Part1 = SparkFun ESP8266 Thing

nets:
  N1: U1.Ground, C1.-, Part1.GND
  N2: U1.Trigger, L1.pin_1
  N3: U1.Output, Part1.ADC
  N4: U1.Discharge, R1.Pin_1, C1.+
  N5: U1.Vcc_Supply_Voltage, R1.Pin_0, Part1.VCC
